# Fritzing sketch TesteAutonomousRobot (saved by Fritzing 0.9.3b)
circuit board: 8.46667cm x 5.64444cm
breadboards: 1

parts:
  Componente1 = Arduino Nano (Rev3.0)
  J1 = Basic Servo
  J3 = Basic Servo
  VCC3 = 4 x AAA Battery Mount
  J6 = Piezo Speaker
  R12 = Resistor [tolerance=±5% resistance=220 package=THT]
  LED2 = LED - 5mm [color="Red (633nm)" package="5 mm [THT]"]
  hc-sr2 = hc-sr04

nets:
  GND: Componente1.GND, J1.gnd, J3.gnd, VCC3.-, J6.pin1, LED2.cathode, hc-sr2.GND
  N1: Componente1.D8, R12.Pin_0
  N2: Componente1.D10, J1.pulse
  N3: Componente1.D11/MOSI, J3.pulse
  N4: Componente1.D12/MISO, J6.pin2
  N5: Componente1.VIN, VCC3.+
  VCC: Componente1.5V, J1.vcc, J3.vcc, hc-sr2.VCC
  N6: Componente1.A3, hc-sr2.Trig
  N7: Componente1.A2, hc-sr2.Echo
  N8: R12.Pin_1, LED2.anode

// code stored in the sketch: NanoRobot.ino
//------------------------------------------------------------------------------------------

#include <Servo.h>//Loads commands to create Servo objects which generate PWM signals

//==================================================
// [S] pino de controle do servo conectado ao pino 7
//==================================================
#define rightServo 10
#define leftServo 11
Servo leftDrive;  // create servo object to control a servo
Servo rightDrive; //another servo object for the left side

int pos = 0;    // variable to store the servo position

void setup()
{
  //  leftDrive.attach(leftServo);  // attaches the servo on pin 9 to the servo object
  //  rightDrive.attach(rightServo);  // attaches the servo on pin 9 to the servo object
}

void loop()
{
  //  //example routine, drives in a square
  //  turnRight();
  //  driveForward();
  //  turnRight();
  //  driveForward();
  //  turnRight();
  //  driveForward();
  //  turnRight();
  //  driveForward();
  //  driveBackward();

  driveForward();
  driveBackward();
  turnRight();
  turnLeft();
}


//the following functions are examples, you could easily make the robot
//move on curved paths or at varying speeds by changing these numbers
//0 is full forward, 90 is stop and 180 is full reverse. The case may be the
//opposite for your build

//drives straight for 1 second
void driveForward()
{
  leftDrive.attach(leftServo);  // attaches the Left Servo on pin 11 to the servo object
  rightDrive.attach(rightServo);  // attaches the Right Servo on pin 10 to the servo object

  leftDrive.write(0);
  rightDrive.write(180);

  delay(5000);

  leftDrive.detach();
  rightDrive.detach();
}

//drives straight backward for 1 second
void driveBackward()
{
  leftDrive.attach(leftServo);  // attaches the Left Servo on pin 11 to the servo object
  rightDrive.attach(rightServo);  // attaches the Right Servo on pin 10 to the servo object

  leftDrive.write(180);
  rightDrive.write(0);

  delay(5000);

  leftDrive.detach();
  rightDrive.detach();
}

//turns right about 90 degrees
void turnRight()
{
  leftDrive.attach(leftServo);  // attaches the Left Servo on pin 11 to the servo object
  rightDrive.attach(rightServo);  // attaches the Right Servo on pin 10 to the servo object

  leftDrive.write(0);
  rightDrive.write(0);

  delay(450);

  leftDrive.detach();
  rightDrive.detach();
}

//turns left about 90 degrees
void turnLeft()
{
  leftDrive.attach(leftServo);  // attaches the Left Servo on pin 11 to the servo object
  rightDrive.attach(rightServo);  // attaches the Right Servo on pin 10 to the servo object

  leftDrive.write(180);
  rightDrive.write(180);

  delay(450);

  leftDrive.detach();
  rightDrive.detach();
}

//end code---------------------------------------------
