# Fritzing sketch Teste_Bluetooth (saved by Fritzing 0.9.3b)
circuit board: 8.46667cm x 5.64444cm
breadboards: 1

parts:
  Componente1 = Arduino Nano (Rev3.0)
  VCC3 = 4 x AAA Battery Mount
  J6 = Piezo Speaker
  R12 = Resistor [tolerance=±5% resistance=220 package=THT]
  LED2 = LED - 5mm [color="Red (633nm)" package="5 mm [THT]"]
  Componente6 = Bluetooth HC-05 Macho
  R13 = Resistor [tolerance=±5% resistance=1k package=THT]
  R15 = Resistor [tolerance=±5% resistance=1k package=THT]
  R16 = Resistor [tolerance=±5% resistance=1k package=THT]

nets:
  GND: Componente1.GND, VCC3.-, J6.pin1, LED2.cathode, Componente6.GND, R13.Pin_1
  N1: Componente1.D5, Componente6.TXD
  N2: Componente1.D6, R15.Pin_0
  N3: Componente1.D8, R12.Pin_0
  N4: Componente1.D12/MISO, J6.pin2
  N5: Componente1.VIN, VCC3.+
  5V: Componente1.5V, Componente6.VCC
  N6: R12.Pin_1, LED2.anode
  N7: Componente6.RXD, R15.Pin_1, R16.Pin_0
  N8: R13.Pin_0, R16.Pin_1

// code stored in the sketch: NanoRobot.ino
//------------------------------------------------------------------------------------------

#include <Servo.h>//Loads commands to create Servo objects which generate PWM signals

//==================================================
// [S] pino de controle do servo conectado ao pino 7
//==================================================
#define rightServo 10
#define leftServo 11
Servo leftDrive;  // create servo object to control a servo
Servo rightDrive; //another servo object for the left side

int pos = 0;    // variable to store the servo position

void setup()
{
  //  leftDrive.attach(leftServo);  // attaches the servo on pin 9 to the servo object
  //  rightDrive.attach(rightServo);  // attaches the servo on pin 9 to the servo object
}

void loop()
{
  //  //example routine, drives in a square
  //  turnRight();
  //  driveForward();
  //  turnRight();
  //  driveForward();
  //  turnRight();
  //  driveForward();
  //  turnRight();
  //  driveForward();
  //  driveBackward();

  driveForward();
  driveBackward();
  turnRight();
  turnLeft();
}


//the following functions are examples, you could easily make the robot
//move on curved paths or at varying speeds by changing these numbers
//0 is full forward, 90 is stop and 180 is full reverse. The case may be the
//opposite for your build

//drives straight for 1 second
void driveForward()
{
  leftDrive.attach(leftServo);  // attaches the Left Servo on pin 11 to the servo object
  rightDrive.attach(rightServo);  // attaches the Right Servo on pin 10 to the servo object

  leftDrive.write(0);
  rightDrive.write(180);

  delay(5000);

  leftDrive.detach();
  rightDrive.detach();
}

//drives straight backward for 1 second
void driveBackward()
{
  leftDrive.attach(leftServo);  // attaches the Left Servo on pin 11 to the servo object
  rightDrive.attach(rightServo);  // attaches the Right Servo on pin 10 to the servo object

  leftDrive.write(180);
  rightDrive.write(0);

  delay(5000);

  leftDrive.detach();
  rightDrive.detach();
}

//turns right about 90 degrees
void turnRight()
{
  leftDrive.attach(leftServo);  // attaches the Left Servo on pin 11 to the servo object
  rightDrive.attach(rightServo);  // attaches the Right Servo on pin 10 to the servo object

  leftDrive.write(0);
  rightDrive.write(0);

  delay(450);

  leftDrive.detach();
  rightDrive.detach();
}

//turns left about 90 degrees
void turnLeft()
{
  leftDrive.attach(leftServo);  // attaches the Left Servo on pin 11 to the servo object
  rightDrive.attach(rightServo);  // attaches the Right Servo on pin 10 to the servo object

  leftDrive.write(180);
  rightDrive.write(180);

  delay(450);

  leftDrive.detach();
  rightDrive.detach();
}

//end code---------------------------------------------

// code stored in the sketch: Teste_Bluetooth.ino
//Programa :Testa Bluetooth que Toca Buzina e Música.

/*
                      +-----+
         +------------| USB |------------+
         |            +-----+            |
    B5   | [ ]D13/SCK        MISO/D12[Z] |   B4
         | [ ]3.3V           MOSI/D11[ ]~|   B3
         | [ ]V.ref     ___    SS/D10[ ]~|   B2
    C0   | [ ]A0       / N \       D9[ ]~|   B1
    C1   | [ ]A1      /  A  \      D8[L] |   B0
    C2   | [ ]A2      \  N  /      D7[ ] |   D7
    C3   | [ ]A3       \_0_/       D6[B]~|   D6
    C4   | [ ]A4/SDA               D5[B]~|   D5
    C5   | [ ]A5/SCL               D4[ ] |   D4
         | [ ]A6              INT1/D3[ ]~|   D3
         | [ ]A7              INT0/D2[ ] |   D2
         | [ ]5V                  GND[ ] |
    C6   | [ ]RST                 RST[ ] |   C6
         | [ ]GND   5V MOSI GND   TX1[ ] |   D0
         | [ ]Vin   [ ] [ ] [ ]   RX1[ ] |   D1
         |          [ ] [ ] [ ]          |
         |          MISO SCK RST         |
         | NANO-V3                       |
         +-------------------------------+

         http://busyducks.com/ascii-art-arduinos
*/

#include <SoftwareSerial.h>

//=========================================
// [L] Criando variável para o led vermelho
//=========================================
int LedEstado = 8;

//========================================================
// [B] Bluetooth
// Definição de um objeto SoftwareSerial.
// Usaremos os pinos 5 e 6, como RX e TX, respectivamente.
// Isto evita o erro do Avrdude
//========================================================
SoftwareSerial serial(5, 6);

//================================
// [Z] Buzzer conectado ao pino 12
//================================
int buzzer = 12;

//=======================
// melodia do MARIO THEME
//=======================
int melodia[] = {660, 660, 660, 510, 660, 770, 380};

//=====================
// duração de cada nota
//=====================
int duracaodasnotas[] = {100, 100, 100, 100, 100, 100, 100};

#define LedEstadoCycle 100U
unsigned long LedEstadoLastMillis = 0;
boolean LedEstadoState = false;
char cmd; //Armazena os caracteres enviados pela portal Serial

void setup()
{
  // put your setup code here, to run once:

  //=============================
  // Pino 4 do arduino como saída
  //=============================
  pinMode(LedEstado, OUTPUT);

  //===========================================
  // Sets the baud for serial data transmission
  //===========================================
  serial.begin(9600);

  //==============================
  // Pino 12 do arduino como saída
  //==============================
  pinMode(buzzer, OUTPUT);

}

void loop()
{
  // put your main code here, to run repeatedly:

  // Verifica se chegou algum caractere pela porta serial.
  if (serial.available())
  {
    //==============================================
    // Variável 'cmd' recebe o valor da porta Serial
    //==============================================
    cmd = serial.read();

    switch (cmd)
    {
      case 'A' : //Acende o LED
        //Mensagem será enviada para o módulo HC-06 e daí para o Android.
        serial.println("Acende o LED");
        digitalWrite(LedEstado, HIGH);
        break;

      case 'a' : //Apaga o LED
        //Mensagem será enviada para o módulo HC-06 e daí para o Android.
        serial.println("Apaga o LED");
        digitalWrite(LedEstado, LOW);
        break;

      case 'P' : //Se 'P' for recebido, Pisca o Led de Estado
        //Mensagem será enviada para o módulo HC-06 e daí para o Android.
        serial.print("Pisca LED");
        piscaLed();
        break;

      case 'B' : //Se 'B' for recebido, Toca a Buzina
        //Mensagem será enviada para o módulo HC-06 e daí para o Android.
        serial.print("Play the Buzzer");

        //Play the Buzzer
        playBuzzer();

        break;

      case 'M' : //Se 'M' for recebido, Toca a Música
        //Mensagem será enviada para o módulo HC-06 e daí para o Android.
        serial.print("Play the Music");

        //Play Super Mario Theme
        playSuperMarioTheme();
        break;
    }
  }
}

void pausa(unsigned int milisegundos)
{
  volatile unsigned long compara = 0;
  volatile int contador = 0;
  do
  {
    if (compara != millis())
    {
      contador++;
      compara = millis();
    }
  } while (contador <= milisegundos);
  return;
}

void playBuzzer()
{
  /*
    o número 12 indica que o pino positivo do buzzer está na porta 12
    o número 300 é a frequência que será tocada
    o número 300 é a duração do som
  */

  //==============
  //aqui sai o som
  //==============
  tone(buzzer, 300, 300);
  pausa(500);

  //==============
  //aqui sai o som
  //==============
  tone(buzzer, 100, 300);
  pausa(500);

  //==============
  //aqui sai o som
  //==============
  tone(buzzer, 900, 300);
  pausa(500);
}

void playSuperMarioTheme()
{
  //for para tocar as 6 primeiras notas, começando no 0 ate 6 ++ incrementado
  for (int nota = 0; nota < 6; nota++)
  {
    int duracaodanota = duracaodasnotas[nota];
    tone(buzzer, melodia[nota], duracaodanota);

    //pausa depois das notas
    int pausadepoisdasnotas[] = {150, 300, 300, 100, 300, 550, 575};
    pausa(pausadepoisdasnotas[nota]);
  }

  noTone(buzzer);
}

void piscaLed()
{
  digitalWrite(LedEstado, HIGH); //Acende o LED
  pausa(200);
  digitalWrite(LedEstado, LOW); //Apaga o LED
  pausa(200);
  digitalWrite(LedEstado, HIGH); //Acende o LED
  pausa(200);
  digitalWrite(LedEstado, LOW); //Apaga o LED
  pausa(200);
}
