# Fritzing sketch Teste_Sensor_Ultrassonico (saved by Fritzing 0.9.3b)
circuit board: 8.46667cm x 5.64444cm
breadboards: 1

parts:
  Componente1 = Arduino Nano (Rev3.0)
  VCC3 = 4 x AAA Battery Mount
  hc-sr2 = hc-sr04

nets:
  GND: Componente1.GND, VCC3.-, hc-sr2.GND
  N1: Componente1.VIN, VCC3.+
  5V: Componente1.5V, hc-sr2.VCC
  N2: Componente1.A3, hc-sr2.Trig
  N3: Componente1.A2, hc-sr2.Echo

// code stored in the sketch: NanoRobot.ino
//------------------------------------------------------------------------------------------

#include <Servo.h>//Loads commands to create Servo objects which generate PWM signals

//==================================================
// [S] pino de controle do servo conectado ao pino 7
//==================================================
#define rightServo 10
#define leftServo 11
Servo leftDrive;  // create servo object to control a servo
Servo rightDrive; //another servo object for the left side

int pos = 0;    // variable to store the servo position

void setup()
{
  //  leftDrive.attach(leftServo);  // attaches the servo on pin 9 to the servo object
  //  rightDrive.attach(rightServo);  // attaches the servo on pin 9 to the servo object
}

void loop()
{
  //  //example routine, drives in a square
  //  turnRight();
  //  driveForward();
  //  turnRight();
  //  driveForward();
  //  turnRight();
  //  driveForward();
  //  turnRight();
  //  driveForward();
  //  driveBackward();

  driveForward();
  driveBackward();
  turnRight();
  turnLeft();
}


//the following functions are examples, you could easily make the robot
//move on curved paths or at varying speeds by changing these numbers
//0 is full forward, 90 is stop and 180 is full reverse. The case may be the
//opposite for your build

//drives straight for 1 second
void driveForward()
{
  leftDrive.attach(leftServo);  // attaches the Left Servo on pin 11 to the servo object
  rightDrive.attach(rightServo);  // attaches the Right Servo on pin 10 to the servo object

  leftDrive.write(0);
  rightDrive.write(180);

  delay(5000);

  leftDrive.detach();
  rightDrive.detach();
}

//drives straight backward for 1 second
void driveBackward()
{
  leftDrive.attach(leftServo);  // attaches the Left Servo on pin 11 to the servo object
  rightDrive.attach(rightServo);  // attaches the Right Servo on pin 10 to the servo object

  leftDrive.write(180);
  rightDrive.write(0);

  delay(5000);

  leftDrive.detach();
  rightDrive.detach();
}

//turns right about 90 degrees
void turnRight()
{
  leftDrive.attach(leftServo);  // attaches the Left Servo on pin 11 to the servo object
  rightDrive.attach(rightServo);  // attaches the Right Servo on pin 10 to the servo object

  leftDrive.write(0);
  rightDrive.write(0);

  delay(450);

  leftDrive.detach();
  rightDrive.detach();
}

//turns left about 90 degrees
void turnLeft()
{
  leftDrive.attach(leftServo);  // attaches the Left Servo on pin 11 to the servo object
  rightDrive.attach(rightServo);  // attaches the Right Servo on pin 10 to the servo object

  leftDrive.write(180);
  rightDrive.write(180);

  delay(450);

  leftDrive.detach();
  rightDrive.detach();
}

//end code---------------------------------------------

// code stored in the sketch: Teste_Sensor_Ultrassonico.ino
/* Criado por Ronilson Santos em 17/07/2014
* Testes realizados com sucesso. 
*/


/*
                      +-----+
         +------------| USB |------------+
         |            +-----+            |
    B5   | [ ]D13/SCK        MISO/D12[ ] |   B4
         | [ ]3.3V           MOSI/D11[ ]~|   B3
         | [ ]V.ref     ___    SS/D10[ ]~|   B2
    C0   | [ ]A0       / N \       D9[ ]~|   B1
    C1   | [ ]A1      /  A  \      D8[ ] |   B0
    C2   | [ ]A2      \  N  /      D7[ ] |   D7
    C3   | [ ]A3       \_0_/       D6[ ]~|   D6
    C4   | [D]A4/SDA               D5[ ]~|   D5
    C5   | [D]A5/SCL               D4[ ] |   D4
         | [ ]A6              INT1/D3[ ]~|   D3
         | [ ]A7              INT0/D2[ ] |   D2
         | [ ]5V                  GND[ ] |
    C6   | [ ]RST                 RST[ ] |   C6
         | [ ]GND   5V MOSI GND   TX1[ ] |   D0
         | [ ]Vin   [ ] [ ] [ ]   RX1[ ] |   D1
         |          [ ] [ ] [ ]          |
         |          MISO SCK RST         |
         | NANO-V3                       |
         +-------------------------------+

         http://busyducks.com/ascii-art-arduinos
*/

/*
  HC-SR04 NewPing Library Demonstration
  HC-SR04-NewPing.ino
  Demonstrates functions of NewPing Library for HC-SR04 Ultrasonic Range Finder
  Displays results on Serial Monitor

  DroneBot Workshop 2017
  http://dronebotworkshop.com
*/

// This uses Serial Monitor to display Range Finder distance readings

// Include NewPing Library
#include "NewPing.h"

// Hook up HC-SR04 with Trig to Arduino Pin 10, Echo to Arduino pin 13
// Maximum Distance is 400 cm

#define TRIGGER_PIN  A4
#define ECHO_PIN     A5
#define MAX_DISTANCE 400
 
NewPing sonar(TRIGGER_PIN, ECHO_PIN, MAX_DISTANCE);

float distance;

void setup() {
  Serial.begin (9600);
}

void loop() {
   
  distance = sonar.ping_cm();
  
  // Send results to Serial Monitor
  Serial.print("Distance = ");
  if (distance >= 400 || distance <= 2) {
    Serial.println("Out of range");
  }
  else {
    Serial.print(distance);
    Serial.println(" cm");
    delay(500);
  }
  delay(500);
}
